# Fritzing sketch EmergencyButton (saved by Fritzing 0.9.3b)

parts:
  S2 = Pushbutton [package="[THT]"]
  WeMos_D1_Mini1 = WeMos D1 Mini
  U1 = LIPO-110mAh [package=lipo-110]
  100k = Resistor [tolerance=±5% resistance=100k package="0402 [SMD]"]
  R1 = Resistor [tolerance=±5% resistance=100k package=THT]

nets:
  N1: S2.Pin_3, S2.Pin_4, WeMos_D1_Mini1.G, WeMos_D1_Mini1.RST, U1.-, R1.Pin_1
  N2: WeMos_D1_Mini1.3V3, R1.Pin_0
  N3: WeMos_D1_Mini1.5V, U1.+, 100k.Pin_1
  N4: WeMos_D1_Mini1.A0, 100k.Pin_0
